// Logisim project logical connectives.circ as structural Verilog: 1 circuit, main circuit main
module main (
  input  in_1,
  input  P,
  input  Q,
  input  P_2,
  input  Q_2,
  input  P_3,
  input  Q_3,
  input  P_4,
  input  Q_4,
  input  P_5,
  input  Q_5
);

  wire and_1_out, not_1_out, not_2_out, or_1_out, or_2_out, xnor_1_out, xor_1_out;

  not not_1 (not_1_out, P_5);
  LED led_1 (.in(not_2_out));
  not not_2 (not_2_out, in_1);
  LED led_2 (.in(and_1_out));
  and and_1 (and_1_out, P, Q);
  LED led_3 (.in(or_1_out));
  or or_1 (or_1_out, P_2, Q_2);
  LED led_4 (.in(xor_1_out));
  xor xor_1 (xor_1_out, P_3, Q_3);
  xnor xnor_1 (xnor_1_out, P_4, Q_4);
  LED led_5 (.in(xnor_1_out));
  or or_2 (or_2_out, not_1_out, Q_5);
  LED led_6 (.in(or_2_out));

  // Notes on the sheet:
  //   NEGATION
  //   CONJUCTION
  //   DISJUNCTION
  //   EXCUSIVE OR
  //   BICONDITIONAL
  //   IMPLICATION
endmodule
