// Logisim project sample.circ as structural Verilog: 1 circuit, main circuit main
module main (
  input  P,
  input  Q
);

  wire and_1_out, not_1_out, not_2_out, not_3_out, or_1_out, xor_1_out;

  not not_1 (not_1_out, P);
  and and_1 (and_1_out, P, Q);
  not not_2 (not_2_out, Q);
  xor xor_1 (xor_1_out, Q, not_1_out);
  not not_3 (not_3_out, and_1_out);
  or or_1 (or_1_out, not_2_out, xor_1_out);
  // OR_Gate or_2 has open pins: in1=not_3_out, in3=or_1_out, out=open
endmodule
